# Fritzing sketch Keyboard (saved by Fritzing 0.9.3b)

parts:
  Esc = Cherry MX Keyswitch
  F1 = Cherry MX Keyswitch
  F2 = Cherry MX Keyswitch
  F3 = Cherry MX Keyswitch
  D1 = Zener Diode [part_number=1N4148 breakdown_voltage=3.6V package="300 mil [THT]"]
  D2 = Zener Diode [part_number=1N4148 breakdown_voltage=3.6V package="300 mil [THT]"]
  D3 = Zener Diode [part_number=1N4148 breakdown_voltage=3.6V package="300 mil [THT]"]
  D4 = Zener Diode [part_number=1N4148 breakdown_voltage=3.6V package="300 mil [THT]"]
  F4 = Cherry MX Keyswitch
  D5 = Zener Diode [part_number=1N4148 breakdown_voltage=3.6V package="300 mil [THT]"]
  F5 = Cherry MX Keyswitch
  D6 = Zener Diode [part_number=1N4148 breakdown_voltage=3.6V package="300 mil [THT]"]
  F6 = Cherry MX Keyswitch
  D7 = Zener Diode [part_number=1N4148 breakdown_voltage=3.6V package="300 mil [THT]"]
  F7 = Cherry MX Keyswitch
  D8 = Zener Diode [part_number=1N4148 breakdown_voltage=3.6V package="300 mil [THT]"]
  F8 = Cherry MX Keyswitch
  D9 = Zener Diode [part_number=1N4148 breakdown_voltage=3.6V package="300 mil [THT]"]
  F9 = Cherry MX Keyswitch
  D10 = Zener Diode [part_number=1N4148 breakdown_voltage=3.6V package="300 mil [THT]"]
  F10 = Cherry MX Keyswitch
  D11 = Zener Diode [part_number=1N4148 breakdown_voltage=3.6V package="300 mil [THT]"]
  F12 = Cherry MX Keyswitch
  F11 = Cherry MX Keyswitch
  D12 = Zener Diode [part_number=1N4148 breakdown_voltage=3.6V package="300 mil [THT]"]
  D13 = Zener Diode [part_number=1N4148 breakdown_voltage=3.6V package="300 mil [THT]"]
  Scroll_Lock = Cherry MX Keyswitch
  Pause/Break = Cherry MX Keyswitch
  Print_Screen = Cherry MX Keyswitch
  D14 = Zener Diode [part_number=1N4148 breakdown_voltage=3.6V package="300 mil [THT]"]
  D15 = Zener Diode [part_number=1N4148 breakdown_voltage=3.6V package="300 mil [THT]"]
  D16 = Zener Diode [part_number=1N4148 breakdown_voltage=3.6V package="300 mil [THT]"]
  Home = Cherry MX Keyswitch
  Page_Up = Cherry MX Keyswitch
  Insert = Cherry MX Keyswitch
  D17 = Zener Diode [part_number=1N4148 breakdown_voltage=3.6V package="300 mil [THT]"]
  D18 = Zener Diode [part_number=1N4148 breakdown_voltage=3.6V package="300 mil [THT]"]
  D19 = Zener Diode [part_number=1N4148 breakdown_voltage=3.6V package="300 mil [THT]"]
  End = Cherry MX Keyswitch
  Page_Down = Cherry MX Keyswitch
  Delete = Cherry MX Keyswitch
  D20 = Zener Diode [part_number=1N4148 breakdown_voltage=3.6V package="300 mil [THT]"]
  D21 = Zener Diode [part_number=1N4148 breakdown_voltage=3.6V package="300 mil [THT]"]
  D22 = Zener Diode [part_number=1N4148 breakdown_voltage=3.6V package="300 mil [THT]"]
  Down = Cherry MX Keyswitch
  Right = Cherry MX Keyswitch
  Left = Cherry MX Keyswitch
  D23 = Zener Diode [part_number=1N4148 breakdown_voltage=3.6V package="300 mil [THT]"]
  D24 = Zener Diode [part_number=1N4148 breakdown_voltage=3.6V package="300 mil [THT]"]
  D25 = Zener Diode [part_number=1N4148 breakdown_voltage=3.6V package="300 mil [THT]"]
  Up = Cherry MX Keyswitch
  D26 = Zener Diode [part_number=1N4148 breakdown_voltage=3.6V package="300 mil [THT]"]
  Num_Lock = Cherry MX Keyswitch
  D27 = Zener Diode [part_number=1N4148 breakdown_voltage=3.6V package="300 mil [THT]"]
  / = Cherry MX Keyswitch
  D28 = Zener Diode [part_number=1N4148 breakdown_voltage=3.6V package="300 mil [THT]"]
  * = Cherry MX Keyswitch
  D29 = Zener Diode [part_number=1N4148 breakdown_voltage=3.6V package="300 mil [THT]"]
  - = Cherry MX Keyswitch
  D30 = Zener Diode [part_number=1N4148 breakdown_voltage=3.6V package="300 mil [THT]"]
  + = Cherry MX Keyswitch
  9/Page_Up = Cherry MX Keyswitch
  7/Home = Cherry MX Keyswitch  # not connected
  8/Up = Cherry MX Keyswitch
  D31 = Zener Diode [part_number=1N4148 breakdown_voltage=3.6V package="300 mil [THT]"]
  D32 = Zener Diode [part_number=1N4148 breakdown_voltage=3.6V package="300 mil [THT]"]
  D33 = Zener Diode [part_number=1N4148 breakdown_voltage=3.6V package="300 mil [THT]"]
  D34 = Zener Diode [part_number=1N4148 breakdown_voltage=3.6V package="300 mil [THT]"]  # not connected
  6/Right = Cherry MX Keyswitch
  4/Left = Cherry MX Keyswitch
  5 = Cherry MX Keyswitch
  D35 = Zener Diode [part_number=1N4148 breakdown_voltage=3.6V package="300 mil [THT]"]
  D36 = Zener Diode [part_number=1N4148 breakdown_voltage=3.6V package="300 mil [THT]"]
  D37 = Zener Diode [part_number=1N4148 breakdown_voltage=3.6V package="300 mil [THT]"]
  3/Page_Down = Cherry MX Keyswitch
  1/End = Cherry MX Keyswitch
  2/Down = Cherry MX Keyswitch
  D38 = Zener Diode [part_number=1N4148 breakdown_voltage=3.6V package="300 mil [THT]"]
  D39 = Zener Diode [part_number=1N4148 breakdown_voltage=3.6V package="300 mil [THT]"]
  D40 = Zener Diode [part_number=1N4148 breakdown_voltage=3.6V package="300 mil [THT]"]
  Return = Cherry MX Keyswitch
  0/Insert = Cherry MX Keyswitch
  /Delete = Cherry MX Keyswitch
  D41 = Zener Diode [part_number=1N4148 breakdown_voltage=3.6V package="300 mil [THT]"]
  D42 = Zener Diode [part_number=1N4148 breakdown_voltage=3.6V package="300 mil [THT]"]
  D43 = Zener Diode [part_number=1N4148 breakdown_voltage=3.6V package="300 mil [THT]"]
  Spacebar = Cherry MX Keyswitch  # not connected
  D44 = Zener Diode [part_number=1N4148 breakdown_voltage=3.6V package="300 mil [THT]"]  # not connected
  RightCTRL = Cherry MX Keyswitch  # not connected
  D45 = Zener Diode [part_number=1N4148 breakdown_voltage=3.6V package="300 mil [THT]"]  # not connected
  RightClick = Cherry MX Keyswitch  # not connected
  D46 = Zener Diode [part_number=1N4148 breakdown_voltage=3.6V package="300 mil [THT]"]  # not connected
  FN = Cherry MX Keyswitch  # not connected
  D47 = Zener Diode [part_number=1N4148 breakdown_voltage=3.6V package="300 mil [THT]"]  # not connected
  Alt = Cherry MX Keyswitch  # not connected
  D48 = Zener Diode [part_number=1N4148 breakdown_voltage=3.6V package="300 mil [THT]"]  # not connected
  Alt_2 = Cherry MX Keyswitch  # not connected
  D49 = Zener Diode [part_number=1N4148 breakdown_voltage=3.6V package="300 mil [THT]"]  # not connected
  OS = Cherry MX Keyswitch  # not connected
  D50 = Zener Diode [part_number=1N4148 breakdown_voltage=3.6V package="300 mil [THT]"]  # not connected
  LeftCTRL = Cherry MX Keyswitch  # not connected
  D51 = Zener Diode [part_number=1N4148 breakdown_voltage=3.6V package="300 mil [THT]"]  # not connected
  Shift = Cherry MX Keyswitch  # not connected
  D52 = Zener Diode [part_number=1N4148 breakdown_voltage=3.6V package="300 mil [THT]"]  # not connected
  Enter = Cherry MX Keyswitch  # not connected
  D53 = Zener Diode [part_number=1N4148 breakdown_voltage=3.6V package="300 mil [THT]"]  # not connected
  \/| = Cherry MX Keyswitch  # not connected
  D54 = Zener Diode [part_number=1N4148 breakdown_voltage=3.6V package="300 mil [THT]"]  # not connected
  Backspace = Cherry MX Keyswitch  # not connected
  D55 = Zener Diode [part_number=1N4148 breakdown_voltage=3.6V package="300 mil [THT]"]  # not connected
  //? = Cherry MX Keyswitch  # not connected
  D56 = Zener Diode [part_number=1N4148 breakdown_voltage=3.6V package="300 mil [THT]"]  # not connected
  '/" = Cherry MX Keyswitch  # not connected
  D57 = Zener Diode [part_number=1N4148 breakdown_voltage=3.6V package="300 mil [THT]"]  # not connected
  ]/} = Cherry MX Keyswitch  # not connected
  D58 = Zener Diode [part_number=1N4148 breakdown_voltage=3.6V package="300 mil [THT]"]  # not connected
  =/+ = Cherry MX Keyswitch  # not connected
  D59 = Zener Diode [part_number=1N4148 breakdown_voltage=3.6V package="300 mil [THT]"]  # not connected
  -/ = Cherry MX Keyswitch  # not connected
  D60 = Zener Diode [part_number=1N4148 breakdown_voltage=3.6V package="300 mil [THT]"]  # not connected
  [/{ = Cherry MX Keyswitch  # not connected
  D61 = Zener Diode [part_number=1N4148 breakdown_voltage=3.6V package="300 mil [THT]"]  # not connected
  ;/ = Cherry MX Keyswitch  # not connected
  D62 = Zener Diode [part_number=1N4148 breakdown_voltage=3.6V package="300 mil [THT]"]  # not connected
  /> = Cherry MX Keyswitch  # not connected
  D63 = Zener Diode [part_number=1N4148 breakdown_voltage=3.6V package="300 mil [THT]"]  # not connected
  /< = Cherry MX Keyswitch  # not connected
  D64 = Zener Diode [part_number=1N4148 breakdown_voltage=3.6V package="300 mil [THT]"]  # not connected
  Shift_2 = Cherry MX Keyswitch  # not connected
  D65 = Zener Diode [part_number=1N4148 breakdown_voltage=3.6V package="300 mil [THT]"]  # not connected
  CapsLock = Cherry MX Keyswitch  # not connected
  D66 = Zener Diode [part_number=1N4148 breakdown_voltage=3.6V package="300 mil [THT]"]  # not connected
  Tab = Cherry MX Keyswitch  # not connected
  D67 = Zener Diode [part_number=1N4148 breakdown_voltage=3.6V package="300 mil [THT]"]  # not connected
  `/~ = Cherry MX Keyswitch  # not connected
  D68 = Zener Diode [part_number=1N4148 breakdown_voltage=3.6V package="300 mil [THT]"]  # not connected
  1/! = Cherry MX Keyswitch  # not connected
  D69 = Zener Diode [part_number=1N4148 breakdown_voltage=3.6V package="300 mil [THT]"]  # not connected
  2/@ = Cherry MX Keyswitch  # not connected
  D70 = Zener Diode [part_number=1N4148 breakdown_voltage=3.6V package="300 mil [THT]"]  # not connected
  3/# = Cherry MX Keyswitch  # not connected
  D71 = Zener Diode [part_number=1N4148 breakdown_voltage=3.6V package="300 mil [THT]"]  # not connected
  4/$ = Cherry MX Keyswitch  # not connected
  D72 = Zener Diode [part_number=1N4148 breakdown_voltage=3.6V package="300 mil [THT]"]  # not connected
  5/% = Cherry MX Keyswitch  # not connected
  D73 = Zener Diode [part_number=1N4148 breakdown_voltage=3.6V package="300 mil [THT]"]  # not connected
  6/^ = Cherry MX Keyswitch  # not connected
  D74 = Zener Diode [part_number=1N4148 breakdown_voltage=3.6V package="300 mil [THT]"]  # not connected
  7/& = Cherry MX Keyswitch  # not connected
  D75 = Zener Diode [part_number=1N4148 breakdown_voltage=3.6V package="300 mil [THT]"]  # not connected
  8/* = Cherry MX Keyswitch  # not connected
  D76 = Zener Diode [part_number=1N4148 breakdown_voltage=3.6V package="300 mil [THT]"]  # not connected
  9/( = Cherry MX Keyswitch  # not connected
  D77 = Zener Diode [part_number=1N4148 breakdown_voltage=3.6V package="300 mil [THT]"]  # not connected
  0/) = Cherry MX Keyswitch  # not connected
  D78 = Zener Diode [part_number=1N4148 breakdown_voltage=3.6V package="300 mil [THT]"]  # not connected
  Q = Cherry MX Keyswitch  # not connected
  D79 = Zener Diode [part_number=1N4148 breakdown_voltage=3.6V package="300 mil [THT]"]  # not connected
  W = Cherry MX Keyswitch  # not connected
  D80 = Zener Diode [part_number=1N4148 breakdown_voltage=3.6V package="300 mil [THT]"]  # not connected
  E = Cherry MX Keyswitch  # not connected
  D81 = Zener Diode [part_number=1N4148 breakdown_voltage=3.6V package="300 mil [THT]"]  # not connected
  R = Cherry MX Keyswitch  # not connected
  D82 = Zener Diode [part_number=1N4148 breakdown_voltage=3.6V package="300 mil [THT]"]  # not connected
  T = Cherry MX Keyswitch  # not connected
  D83 = Zener Diode [part_number=1N4148 breakdown_voltage=3.6V package="300 mil [THT]"]  # not connected
  Y = Cherry MX Keyswitch  # not connected
  D84 = Zener Diode [part_number=1N4148 breakdown_voltage=3.6V package="300 mil [THT]"]  # not connected
  U = Cherry MX Keyswitch  # not connected
  D85 = Zener Diode [part_number=1N4148 breakdown_voltage=3.6V package="300 mil [THT]"]  # not connected
  I = Cherry MX Keyswitch  # not connected
  D86 = Zener Diode [part_number=1N4148 breakdown_voltage=3.6V package="300 mil [THT]"]  # not connected
  O = Cherry MX Keyswitch  # not connected
  D87 = Zener Diode [part_number=1N4148 breakdown_voltage=3.6V package="300 mil [THT]"]  # not connected
  P = Cherry MX Keyswitch  # not connected
  D88 = Zener Diode [part_number=1N4148 breakdown_voltage=3.6V package="300 mil [THT]"]  # not connected
  A = Cherry MX Keyswitch  # not connected
  D89 = Zener Diode [part_number=1N4148 breakdown_voltage=3.6V package="300 mil [THT]"]  # not connected
  S = Cherry MX Keyswitch  # not connected
  D90 = Zener Diode [part_number=1N4148 breakdown_voltage=3.6V package="300 mil [THT]"]  # not connected
  D = Cherry MX Keyswitch  # not connected
  D91 = Zener Diode [part_number=1N4148 breakdown_voltage=3.6V package="300 mil [THT]"]  # not connected
  F = Cherry MX Keyswitch  # not connected
  D92 = Zener Diode [part_number=1N4148 breakdown_voltage=3.6V package="300 mil [THT]"]  # not connected
  G = Cherry MX Keyswitch  # not connected
  D93 = Zener Diode [part_number=1N4148 breakdown_voltage=3.6V package="300 mil [THT]"]  # not connected
  H = Cherry MX Keyswitch  # not connected
  D94 = Zener Diode [part_number=1N4148 breakdown_voltage=3.6V package="300 mil [THT]"]  # not connected
  J = Cherry MX Keyswitch  # not connected
  D95 = Zener Diode [part_number=1N4148 breakdown_voltage=3.6V package="300 mil [THT]"]  # not connected
  K = Cherry MX Keyswitch  # not connected
  D96 = Zener Diode [part_number=1N4148 breakdown_voltage=3.6V package="300 mil [THT]"]  # not connected
  L = Cherry MX Keyswitch  # not connected
  D97 = Zener Diode [part_number=1N4148 breakdown_voltage=3.6V package="300 mil [THT]"]  # not connected
  Z = Cherry MX Keyswitch  # not connected
  D98 = Zener Diode [part_number=1N4148 breakdown_voltage=3.6V package="300 mil [THT]"]  # not connected
  X = Cherry MX Keyswitch  # not connected
  D99 = Zener Diode [part_number=1N4148 breakdown_voltage=3.6V package="300 mil [THT]"]  # not connected
  C = Cherry MX Keyswitch  # not connected
  D100 = Zener Diode [part_number=1N4148 breakdown_voltage=3.6V package="300 mil [THT]"]  # not connected
  V = Cherry MX Keyswitch  # not connected
  D101 = Zener Diode [part_number=1N4148 breakdown_voltage=3.6V package="300 mil [THT]"]  # not connected
  B = Cherry MX Keyswitch  # not connected
  D102 = Zener Diode [part_number=1N4148 breakdown_voltage=3.6V package="300 mil [THT]"]  # not connected
  N = Cherry MX Keyswitch  # not connected
  D103 = Zener Diode [part_number=1N4148 breakdown_voltage=3.6V package="300 mil [THT]"]  # not connected
  M = Cherry MX Keyswitch  # not connected
  D104 = Zener Diode [part_number=1N4148 breakdown_voltage=3.6V package="300 mil [THT]"]  # not connected

nets:
  N1: Esc.pin_4, D1.anode
  N2: F1.pin_4, D2.anode
  N3: F2.pin_4, D3.anode
  N4: F3.pin_4, D4.anode
  N5: F4.pin_4, D5.anode
  N6: F5.pin_4, D6.anode
  N7: F6.pin_4, D7.anode
  N8: F7.pin_4, D8.anode
  N9: F8.pin_4, D9.anode
  N10: F9.pin_4, D10.anode
  N11: F10.pin_4, D11.anode
  N12: F12.pin_4, D13.anode
  N13: F11.pin_4, D12.anode
  N14: Scroll_Lock.pin_4, D15.anode
  N15: Pause/Break.pin_4, D14.anode
  N16: Print_Screen.pin_4, D16.anode
  N17: Home.pin_4, D18.anode
  N18: Page_Up.pin_4, D17.anode
  N19: Insert.pin_4, D19.anode
  N20: End.pin_4, D21.anode
  N21: Page_Down.pin_4, D20.anode
  N22: Delete.pin_4, D22.anode
  N23: Down.pin_4, D24.anode
  N24: Right.pin_4, D23.anode
  N25: Left.pin_4, D25.anode
  N26: Up.pin_4, D26.anode
  N27: Num_Lock.pin_4, D27.anode
  N28: /.pin_4, D28.anode
  N29: *.pin_4, D29.anode
  N30: -.pin_4, D30.anode
  N31: +.pin_4, D31.anode
  N32: 9/Page_Up.pin_4, D32.anode
  N33: 8/Up.pin_4, D33.anode
  N34: 6/Right.pin_4, D35.anode
  N35: 4/Left.pin_4, D37.anode
  N36: 5.pin_4, D36.anode
  N37: 3/Page_Down.pin_4, D38.anode
  N38: 1/End.pin_4, D40.anode
  N39: 2/Down.pin_4, D39.anode
  N40: Return.pin_4, D41.anode
  N41: 0/Insert.pin_4, D43.anode
  N42: /Delete.pin_4, D42.anode
